# Fritzing sketch 도면 (saved by Fritzing 0.9.3b)
breadboards: 1

parts:
  부품1 = Arduino Uno (Rev3)
  R1 = Resistor [tolerance=±5% resistance=10 package=THT]
  LCD1 = LCD screen
  S1 = Pushbutton [package="[THT]"]
  R2 = Rotary Potentiometer (Small) [maximum_resistance=10kΩ package=THT]

nets:
  N1: 부품1.D10_PWM/SS, LCD1.DB4
  N2: 부품1.D11_PWM/MOSI, LCD1.DB5
  N3: 부품1.D12/MISO, LCD1.DB6
  N4: 부품1.D13/SCK, LCD1.DB7
  N5: 부품1.D2, R1.Pin_0, LCD1.DB2, S1.Pin_3, S1.Pin_4
  N6: 부품1.D3_PWM, LCD1.RS
  N7: 부품1.D4, LCD1.E
  5V: 부품1.5V, R1.Pin_1, LCD1.VDD, LCD1.LED+, R2.leg2
  GND: 부품1.GND, LCD1.VSS, LCD1.R/W, LCD1.DB0, LCD1.LED-, S1.Pin_1, S1.Pin_2, R2.leg1
  N8: LCD1.V0, R2.wiper
